// Digital circuit gaming pc.dig as structural Verilog
module gaming_pc (
  input  clk
);

  wire and_1_out, and_2_out, and_3_out, BP_Enable, BP_Write, IP_Conditional_Out, IP_Enable, IP_Write,
       Memory_Load, Memory_Store, Next_Instruction, not_1_out, or_1_out, Reg_A_Read, Reg_A_Write, Reg_B_Read,
       Reg_B_Write, SP_Enable;
  wire [1:0] Address_Select;
  wire [3:0] Stage_Counter_out;
  wire [7:0] _32kx8_RAM_d, Instruction_q, Register_A_q, Register_B_q;
  wire [12:8] Control_ROM_d;
  wire [15:0] Base_Pointer_out, IP_out, multiplexer_1_out, Stack_Pointer_out;

  or or_1 (or_1_out, IP_Write, IP_Conditional_Out);
  Register #(.Bits(8)) Register_A (.D(_32kx8_RAM_d), .C(clk), .en(Reg_A_Write), .Q(Register_A_q));
  Register #(.Bits(8)) Register_B (.D(_32kx8_RAM_d), .C(clk), .en(Reg_B_Write), .Q(Register_B_q));
  CounterPreset #(.Bits(16)) Base_Pointer (
    .en(BP_Enable), .C(clk), .dir(1'b0), .in(multiplexer_1_out), .ld(BP_Write), .clr(1'b0),
    .out(Base_Pointer_out));  // open: ovf
  CounterPreset #(.Bits(16)) Stack_Pointer (
    .en(SP_Enable), .C(clk), .dir(1'b1), .in(multiplexer_1_out), .ld(1'b0), .clr(1'b0),
    .out(Stack_Pointer_out));  // open: ovf
  CounterPreset #(.Bits(16)) IP (
    .en(IP_Enable), .C(clk), .dir(1'b0), .in(multiplexer_1_out), .ld(or_1_out), .clr(1'b0), .out(IP_out));  // open: ovf
  Register #(.Bits(8)) Instruction (.D(_32kx8_RAM_d), .C(clk), .en(Next_Instruction), .Q(Instruction_q));
  Counter #(.Bits(4)) Stage_Counter (.en(1'b1), .C(clk), .clr(Next_Instruction), .out(Stage_Counter_out));  // open: ovf
  // Probe Instruction on Instruction_q
  // Probe Stage on Stage_Counter_out
  Driver #(.Bits(8)) driver_1 (.in(Register_A_q), .en(Reg_A_Read));  // open: out
  Driver #(.Bits(8)) driver_2 (.in(Register_B_q), .en(Reg_B_Read));  // open: out
  Multiplexer #(.Selector_Bits(2), .Bits(16)) multiplexer_1 (
    .sel(Address_Select), .in_0({Register_B_q, Register_A_q}), .in_1(Base_Pointer_out),
    .in_2(Stack_Pointer_out), .in_3(IP_out), .out(multiplexer_1_out));
  ROM #(.AddrBits(12), .isProgramMemory("true"), .Bits(16)) Control_ROM (
    .A({Instruction_q, Stage_Counter_out}), .sel(1'b1),
    .D({Next_Instruction, IP_Enable, IP_Write, Control_ROM_d, Reg_B_Read, Reg_B_Write, Reg_A_Read, Reg_A_Write, Memory_Store, Memory_Load, Address_Select}));
  // Probe Bus on _32kx8_RAM_d
  // Probe Address on multiplexer_1_out
  and and_1 (and_1_out, multiplexer_1_out[15], Memory_Store);
  and and_2 (and_2_out, multiplexer_1_out[15], Memory_Load);
  not not_1 (not_1_out, multiplexer_1_out[15]);
  and and_3 (and_3_out, not_1_out, Memory_Load);
  RAMSinglePort #(.AddrBits(15), .Bits(8)) _32kx8_RAM (
    .A(multiplexer_1_out[14:0]), .str(and_1_out), .C(clk), .ld(and_2_out), .D(_32kx8_RAM_d));
  ROM #(.AddrBits(15), .Bits(8)) _32kx8_ROM (.A(multiplexer_1_out[14:0]), .sel(and_3_out), .D(_32kx8_RAM_d));

  // Notes on the sheet:
  //   contents of Control_ROM (hex, n*v repeats v):
  //   c007,0,0,0,0,0,0,0,0,0,0,0,0,0,0,0,c007,0,0,0,0,0,0,0,0,0,0,0,0,0,0,0,c007,0,0,0,
  //   0,0,0,0,0,0,0,0,0,0,0,0,c007,0,0,0,0,0,0,0,0,0,0,0,0,0,0,0,c007,0,0,0,0,0,0,0,0,0,
  //   0,0,0,0,0,0,c007,0,0,0,0,0,0,0,0,0,0,0,0,0,0,0,c007,0,0,0,0,0,0,0,0,0,0,0,0,0,0,0,
  //   c007,0,0,0,0,0,0,0,0,0,0,0,0,0,0,0,c007,0,0,0,0,0,0,0,0,0,0,0,0,0,0,0,c007,0,0,0,
  //   0,0,0,0,0,0,0,0,0,0,0,0,c007,0,0,0,0,0,0,0,0,0,0,0,0,0,0,0,c007,0,0,0,0,0,0,0,0,0,
  //   0,0,0,0,0,0,c007,0,0,0,0,0,0,0,0,0,0,0,0,0,0,0,c007,0,0,0,0,0,0,0,0,0,0,0,0,0,0,0,
  //   c007,0,0,0,0,0,0,0,0,0,0,0,0,0,0,0,c007,0,0,0,0,0,0,0,0,0,0,0,0,0,0,0,c007,0,0,0,
  //   0,0,0,0,0,0,0,0,0,0,0,0,c007,0,0,0,0,0,0,0,0,0,0,0,0,0,0,0,c007,0,0,0,0,0,0,0,0,0,
  //   0,0,0,0,0,0,c007,0,0,0,0,0,0,0,0,0,0,0,0,0,0,0,c007,0,0,0,0,0,0,0,0,0,0,0,0,0,0,0,
  //   c007,0,0,0,0,0,0,0,0,0,0,0,0,0,0,0,c007,0,0,0,0,0,0,0,0,0,0,0,0,0,0,0,c007,0,0,0,
  //   0,0,0,0,0,0,0,0,0,0,0,0,c007,0,0,0,0,0,0,0,0,0,0,0,0,0,0,0,c007,0,0,0,0,0,0,0,0,0,
  //   0,0,0,0,0,0,c007,0,0,0,0,0,0,0,0,0,0,0,0,0,0,0,c007,0,0,0,0,0,0,0,0,0,0,0,0,0,0,0,
  //   c007,0,0,0,0,0,0,0,0,0,0,0,0,0,0,0,c007,0,0,0,0,0,0,0,0,0,0,0,0,0,0,0,c007,0,0,0,
  //   0,0,0,0,0,0,0,0,0,0,0,0,c007,0,0,0,0,0,0,0,0,0,0,0,0,0,0,0,c007,0,0,0,0,0,0,0,0,0,
  //   0,0,0,0,0,0,c007,0,0,0,0,0,0,0,0,0,0,0,0,0,0,0,c007,0,0,0,0,0,0,0,0,0,0,0,0,0,0,0,
  //   c007,0,0,0,0,0,0,0,0,0,0,0,0,0,0,0,c007,0,0,0,0,0,0,0,0,0,0,0,0,0,0,0,c007,0,0,0,
  //   0,0,0,0,0,0,0,0,0,0,0,0,c007,0,0,0,0,0,0,0,0,0,0,0,0,0,0,0,c007,0,0,0,0,0,0,0,0,0,
  //   0,0,0,0,0,0,c007,0,0,0,0,0,0,0,0,0,0,0,0,0,0,0,c007,0,0,0,0,0,0,0,0,0,0,0,0,0,0,0,
  //   c007,0,0,0,0,0,0,0,0,0,0,0,0,0,0,0,c007,0,0,0,0,0,0,0,0,0,0,0,0,0,0,0,c007,0,0,0,
  //   0,0,0,0,0,0,0,0,0,0,0,0,c007,0,0,0,0,0,0,0,0,0,0,0,0,0,0,0,c007,0,0,0,0,0,0,0,0,0,
  //   0,0,0,0,0,0,c007,0,0,0,0,0,0,0,0,0,0,0,0,0,0,0,c007,0,0,0,0,0,0,0,0,0,0,0,0,0,0,0,
  //   c007,0,0,0,0,0,0,0,0,0,0,0,0,0,0,0,c007,0,0,0,0,0,0,0,0,0,0,0,0,0,0,0,c007,0,0,0,
  //   0,0,0,0,0,0,0,0,0,0,0,0,c007,0,0,0,0,0,0,0,0,0,0,0,0,0,0,0,c007,0,0,0,0,0,0,0,0,0,
  //   0,0,0,0,0,0,c007,0,0,0,0,0,0,0,0,0,0,0,0,0,0,0,c007,0,0,0,0,0,0,0,0,0,0,0,0,0,0,0,
  //   c007,0,0,0,0,0,0,0,0,0,0,0,0,0,0,0,c007,0,0,0,0,0,0,0,0,0,0,0,0,0,0,0,c007,0,0,0,
  //   0,0,0,0,0,0,0,0,0,0,0,0,c007,0,0,0,0,0,0,0,0,0,0,0,0,0,0,0,c007,0,0,0,0,0,0,0,0,0,
  //   0,0,0,0,0,0,c007,0,0,0,0,0,0,0,0,0,0,0,0,0,0,0,c007,0,0,0,0,0,0,0,0,0,0,0,0,0,0,0,
  //   c007,0,0,0,0,0,0,0,0,0,0,0,0,0,0,0,c007,0,0,0,0,0,0,0,0,0,0,0,0,0,0,0,c007,0,0,0,
  //   0,0,0,0,0,0,0,0,0,0,0,0,c007,0,0,0,0,0,0,0,0,0,0,0,0,0,0,0,c007,0,0,0,0,0,0,0,0,0,
  //   0,0,0,0,0,0,c007,0,0,0,0,0,0,0,0,0,0,0,0,0,0,0,c007,0,0,0,0,0,0,0,0,0,0,0,0,0,0,0,
  //   c007,0,0,0,0,0,0,0,0,0,0,0,0,0,0,0,c007,0,0,0,0,0,0,0,0,0,0,0,0,0,0,0,c007,0,0,0,
  //   0,0,0,0,0,0,0,0,0,0,0,0,c007,0,0,0,0,0,0,0,0,0,0,0,0,0,0,0,c007,0,0,0,0,0,0,0,0,0,
  //   0,0,0,0,0,0,c007,0,0,0,0,0,0,0,0,0,0,0,0,0,0,0,c007,0,0,0,0,0,0,0,0,0,0,0,0,0,0,0,
  //   c007,0,0,0,0,0,0,0,0,0,0,0,0,0,0,0,c007,0,0,0,0,0,0,0,0,0,0,0,0,0,0,0,c007,0,0,0,
  //   0,0,0,0,0,0,0,0,0,0,0,0,c007,0,0,0,0,0,0,0,0,0,0,0,0,0,0,0,c007,0,0,0,0,0,0,0,0,0,
  //   0,0,0,0,0,0,c007,0,0,0,0,0,0,0,0,0,0,0,0,0,0,0,c007,0,0,0,0,0,0,0,0,0,0,0,0,0,0,0,
  //   c007,0,0,0,0,0,0,0,0,0,0,0,0,0,0,0,c007,0,0,0,0,0,0,0,0,0,0,0,0,0,0,0,c007,0,0,0,
  //   0,0,0,0,0,0,0,0,0,0,0,0,c007,0,0,0,0,0,0,0,0,0,0,0,0,0,0,0,c007,0,0,0,0,0,0,0,0,0,
  //   0,0,0,0,0,0,c007,0,0,0,0,0,0,0,0,0,0,0,0,0,0,0,c007,0,0,0,0,0,0,0,0,0,0,0,0,0,0,0,
  //   c007,0,0,0,0,0,0,0,0,0,0,0,0,0,0,0,c007,0,0,0,0,0,0,0,0,0,0,0,0,0,0,0,c007,0,0,0,
  //   0,0,0,0,0,0,0,0,0,0,0,0,c007,0,0,0,0,0,0,0,0,0,0,0,0,0,0,0,c007,0,0,0,0,0,0,0,0,0,
  //   0,0,0,0,0,0,c007,0,0,0,0,0,0,0,0,0,0,0,0,0,0,0,c007,0,0,0,0,0,0,0,0,0,0,0,0,0,0,0,
  //   c007,0,0,0,0,0,0,0,0,0,0,0,0,0,0,0,c007,0,0,0,0,0,0,0,0,0,0,0,0,0,0,0,c007,0,0,0,
  //   0,0,0,0,0,0,0,0,0,0,0,0,c007,0,0,0,0,0,0,0,0,0,0,0,0,0,0,0,c007,0,0,0,0,0,0,0,0,0,
  //   0,0,0,0,0,0,c007,0,0,0,0,0,0,0,0,0,0,0,0,0,0,0,c007,0,0,0,0,0,0,0,0,0,0,0,0,0,0,0,
  //   c007,0,0,0,0,0,0,0,0,0,0,0,0,0,0,0,c007,0,0,0,0,0,0,0,0,0,0,0,0,0,0,0,c007,0,0,0,
  //   0,0,0,0,0,0,0,0,0,0,0,0,c007,0,0,0,0,0,0,0,0,0,0,0,0,0,0,0,c007,0,0,0,0,0,0,0,0,0,
  //   0,0,0,0,0,0,c007,0,0,0,0,0,0,0,0,0,0,0,0,0,0,0,c007,0,0,0,0,0,0,0,0,0,0,0,0,0,0,0,
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  //   contents of _32kx8_ROM (hex, n*v repeats v):
  //   0,1,2,3,4,5,6,7,8,9,a,b,c,d,e,f
  //   TODO
  //   - Stack pointer
  //   - up address mux to 3
  //   - put IP on address mux 0
endmodule
